# Fritzing sketch OJOs (saved by Fritzing 0.9.10b)
breadboards: 1

parts:
  Componente1 = Arduino Pro Micro (Clone)
  Componente2 = Matrix LED de 8x8 basada en MAX7219
  Componente3 = Matrix LED de 8x8 basada en MAX7219

nets:
  GND: Componente1.GND, Componente2.GND, Componente3.GND
  N1: Componente1.D10, Componente2.CS
  N2: Componente1.D16, Componente2.CLK
  N3: Componente1.D14, Componente2.DIN
  VCC: Componente1.VCC, Componente2.VCC, Componente3.VCC
  N4: Componente2.CS(OUT), Componente3.CS
  N5: Componente2.CLK(OUT), Componente3.CLK
  N6: Componente2.DOUT, Componente3.DIN
